// Logisim project bladeprod.circ as structural Verilog: 3 circuits, main circuit blademult
module blademult (
  input  [4:0] blade_2,
  input  [4:0] blade_1,
  input  [31:0] in_3,
  input  [31:0] in_4
);

  wire [31:0] n5_to_32_decoder_1_out_6;

  _5_to_32_Decoder u_5_to_32_decoder_1 (
    .s4(blade_2[4]), .s3(blade_2[3]), .s2(blade_2[2]), .s1(blade_2[1]), .s0(blade_2[0]),
    .out_6(n5_to_32_decoder_1_out_6));
  Multiplexer #(.select(5), .width(32), .enable("false")) multiplexer_1 (
    .in0({32{1'b1}}), .sel(blade_1));  // open: in1, in2, in3, in4, in5, in6, in7, in8, in9, in10, in11, in12, in13, in14, in15, in16, in17, in18, in19, in20, in21, in22, in23, in24, in25, in26, in27, in28, in29, in30, in31, out

  // Notes on the sheet:
  //   coefficient 1
  //   coefficient 2
endmodule

module _5_to_32_Decoder (
  input  s4,
  input  s3,
  input  s2,
  input  s1,
  input  s0,
  output [31:0] out_6
);

  wire not_1_out, not_2_out, not_3_out, not_4_out, not_5_out;

  not not_1 (not_1_out, s4);
  not not_2 (not_2_out, s3);
  not not_3 (not_3_out, s2);
  not not_4 (not_4_out, s1);
  not not_5 (not_5_out, s0);
  and _0 (out_6[0], not_5_out, not_4_out, not_3_out, not_2_out, not_1_out);
  and _1 (out_6[1], s0, not_4_out, not_3_out, not_2_out, not_1_out);
  and _2 (out_6[2], not_5_out, s1, not_3_out, not_2_out, not_1_out);
  and _3 (out_6[3], s0, s1, not_3_out, not_2_out, not_1_out);
  and _4 (out_6[4], not_5_out, not_4_out, s2, not_2_out, not_1_out);
  and _5 (out_6[5], s0, not_4_out, s2, not_2_out, not_1_out);
  and _6 (out_6[6], not_5_out, s1, s2, not_2_out, not_1_out);
  and _7 (out_6[7], s0, s1, s2, not_2_out, not_1_out);
  and _8 (out_6[8], not_5_out, not_4_out, not_3_out, s3, not_1_out);
  and _9 (out_6[9], s0, not_4_out, not_3_out, s3, not_1_out);
  and _10 (out_6[10], not_5_out, s1, not_3_out, s3, not_1_out);
  and _11 (out_6[11], s0, s1, not_3_out, s3, not_1_out);
  and _12 (out_6[12], not_5_out, not_4_out, s2, s3, not_1_out);
  and _13 (out_6[13], s0, not_4_out, s2, s3, not_1_out);
  and _14 (out_6[14], not_5_out, s1, s2, s3, not_1_out);
  and _15 (out_6[15], s0, s1, s2, s3, not_1_out);
  and _16 (out_6[16], not_5_out, not_4_out, not_3_out, not_2_out, s4);
  and _17 (out_6[17], s0, not_4_out, not_3_out, not_2_out, s4);
  and _18 (out_6[18], not_5_out, s1, not_3_out, not_2_out, s4);
  and _19 (out_6[19], s0, s1, not_3_out, not_2_out, s4);
  and _20 (out_6[20], not_5_out, not_4_out, s2, not_2_out, s4);
  and _21 (out_6[21], s0, not_4_out, s2, not_2_out, s4);
  and _22 (out_6[22], not_5_out, s1, s2, not_2_out, s4);
  and _23 (out_6[23], s0, s1, s2, not_2_out, s4);
  and _24 (out_6[24], not_5_out, not_4_out, not_3_out, s3, s4);
  and _25 (out_6[25], s0, not_4_out, not_3_out, s3, s4);
  and _26 (out_6[26], not_5_out, s1, not_3_out, s3, s4);
  and _27 (out_6[27], s0, s1, not_3_out, s3, s4);
  and _28 (out_6[28], not_5_out, not_4_out, s2, s3, s4);
  and _29 (out_6[29], s0, not_4_out, s2, s3, s4);
  and _30 (out_6[30], not_5_out, s1, s2, s3, s4);
  and _31 (out_6[31], s0, s1, s2, s3, s4);

  // Notes on the sheet:
  //   Least Significant Bit
  //   Output
endmodule

module conditionalIncrement (
  input  [31:0] in_1,
  input  Enable,
  output [31:0] out_3
);

  wire and_3_out, and_4_out, and_5_out, and_6_out, and_7_out, and_8_out, and_9_out, and_10_out, and_11_out,
       and_12_out, and_13_out, not_1_out, not_2_out, not_3_out, not_4_out, not_5_out, not_6_out, not_7_out,
       not_8_out, not_9_out, not_10_out, not_11_out, not_12_out, not_13_out;

  xor xor_1 (out_3[0], Enable, in_1[0]);
  xor xor_2 (out_3[6], in_1[6], and_4_out);
  not not_1 (not_1_out, out_3[6]);
  and and_1 (out_3[6], not_1_out, in_1[6]);
  not not_2 (not_2_out, out_3[12]);
  // AND_Gate and_2 has open pins: in0=not_2_out, in1=in_1[12], out=open
  not not_3 (not_3_out, out_3[0]);
  and and_3 (and_3_out, not_3_out, in_1[0]);
  and and_4 (and_4_out, in_1[5], not_4_out);
  not not_4 (not_4_out, out_3[9]);
  xor xor_3 (out_3[9], in_1[5], and_5_out);
  xor xor_4 (out_3[7], in_1[7], out_3[6]);
  xor xor_5 (out_3[12], in_1[12], and_7_out);
  xor xor_6 (out_3[1], and_3_out, in_1[1]);
  and and_5 (and_5_out, in_1[4], not_8_out);
  and and_6 (and_6_out, in_1[7], not_5_out);
  not not_5 (not_5_out, out_3[7]);
  and and_7 (and_7_out, in_1[11], not_6_out);
  not not_6 (not_6_out, out_3[11]);
  not not_7 (not_7_out, out_3[1]);
  and and_8 (and_8_out, not_7_out, in_1[1]);
  xor xor_7 (out_3[4], in_1[4], and_12_out);
  not not_8 (not_8_out, out_3[4]);
  xor xor_8 (out_3[8], and_6_out, in_1[8]);
  and and_9 (and_9_out, in_1[10], not_11_out);
  xor xor_9 (out_3[11], in_1[11], and_9_out);
  not not_9 (not_9_out, out_3[2]);
  xor xor_10 (out_3[2], and_8_out, in_1[2]);
  not not_10 (not_10_out, out_3[8]);
  and and_10 (and_10_out, not_10_out, in_1[8]);
  not not_11 (not_11_out, out_3[10]);
  xor xor_11 (out_3[10], in_1[10], and_13_out);
  and and_11 (and_11_out, not_9_out, in_1[2]);
  xor xor_12 (out_3[3], in_1[3], and_11_out);
  not not_12 (not_12_out, out_3[3]);
  and and_12 (and_12_out, in_1[3], not_12_out);
  not not_13 (not_13_out, out_3[9]);
  xor xor_13 (out_3[9], and_10_out, in_1[9]);
  and and_13 (and_13_out, in_1[9], not_13_out);

  assign out_3[5] = out_3[9];

  // Notes on the sheet:
  //   32 bit coefficient
endmodule
